// Logisim project circ7400.circ as structural Verilog: 7 circuits, main circuit main
module main (
);

  _74x00___Quad_2_input_NAND u_74x00_quad_2_input_nand_1 ();  // open: in_1, in_3, out_11, in_6, in_7, out_13, GND, VCC, in_4, in_5, out_12, in_8, in_9, out_14
  _74x244___Octal_tri_state_buffer u_74x244_octal_tri_state_buffer_1 ();  // open: n1G, _1A1, _2Y4, _1A2, _2Y3, _1A3, _2Y2, _1A4, _2Y1, GND, VCC, n2G, _1Y1, _2A4, _1Y2, _2A3, _1Y3, _2A2, _1Y4, _2A1
  _74x02___Quad_2_input_NOR u_74x02_quad_2_input_nor_1 ();  // open: out_11, in_2, in_3, out_13, in_6, in_7, GND, VCC, out_12, in_4, in_5, out_14, in_8, in_10
  _74x04___Hex_NOT u_74x04_hex_not_1 ();  // open: in_1, out_9, in_4, out_11, in_6, out_13, GND, VCC, in_3, out_10, in_5, out_12, in_7, out_14
  _74x08___Quad_2_input_AND u_74x08_quad_2_input_and_1 ();  // open: in_1, in_3, out_11, in_6, in_7, out_13, GND, VCC, in_4, in_5, out_12, in_8, in_9, out_14
  _74x32___Quad_2_input_OR u_74x32_quad_2_input_or_1 ();  // open: in_1, in_3, out_11, in_6, in_7, out_13, GND, VCC, in_4, in_5, out_12, in_8, in_9, out_14
endmodule

// 74x244
module _74x244___Octal_tri_state_buffer (
  input  n1G,
  input  VCC,
  input  _1A1,
  input  n2G,
  input  _1A2,
  input  _2A4,
  input  _1A3,
  input  _2A3,
  input  _1A4,
  input  _2A2,
  input  GND,
  input  _2A1,
  output _2Y4,
  output _1Y1,
  output _2Y3,
  output _1Y2,
  output _2Y2,
  output _1Y3,
  output _2Y1,
  output _1Y4
);

  wire not_1_out, not_2_out;

  not not_1 (not_1_out, n1G);
  assign _1Y1 = not_1_out ? _1A1 : 1'bz;  // Controlled_Buffer controlled_buffer_1
  assign _1Y2 = not_1_out ? _1A2 : 1'bz;  // Controlled_Buffer controlled_buffer_2
  assign _1Y3 = not_1_out ? _1A3 : 1'bz;  // Controlled_Buffer controlled_buffer_3
  assign _1Y4 = not_1_out ? _1A4 : 1'bz;  // Controlled_Buffer controlled_buffer_4
  not not_2 (not_2_out, n2G);
  assign _2Y4 = not_2_out ? _2A4 : 1'bz;  // Controlled_Buffer controlled_buffer_5
  assign _2Y3 = not_2_out ? _2A3 : 1'bz;  // Controlled_Buffer controlled_buffer_6
  assign _2Y2 = not_2_out ? _2A2 : 1'bz;  // Controlled_Buffer controlled_buffer_7
  assign _2Y1 = not_2_out ? _2A1 : 1'bz;  // Controlled_Buffer controlled_buffer_8
endmodule

// 74x00
module _74x00___Quad_2_input_NAND (
  input  in_1,
  input  VCC,
  input  in_3,
  input  in_4,
  input  in_5,
  input  in_6,
  input  in_7,
  input  in_8,
  input  in_9,
  input  GND,
  output out_11,
  output out_12,
  output out_13,
  output out_14
);

  nand nand_1 (out_11, in_3, in_1);
  nand nand_2 (out_13, in_7, in_6);
  nand nand_3 (out_12, in_4, in_5);
  nand nand_4 (out_14, in_8, in_9);
endmodule

// 74x02
module _74x02___Quad_2_input_NOR (
  input  VCC,
  input  in_2,
  input  in_3,
  input  in_4,
  input  in_5,
  input  in_6,
  input  in_7,
  input  in_8,
  input  GND,
  input  in_10,
  output out_11,
  output out_12,
  output out_13,
  output out_14
);

  nor nor_1 (out_11, in_2, in_3);
  nor nor_2 (out_13, in_6, in_7);
  nor nor_3 (out_12, in_5, in_4);
  nor nor_4 (out_14, in_10, in_8);
endmodule

// 74x04
module _74x04___Hex_NOT (
  input  in_1,
  input  VCC,
  input  in_3,
  input  in_4,
  input  in_5,
  input  in_6,
  input  in_7,
  input  GND,
  output out_9,
  output out_10,
  output out_11,
  output out_12,
  output out_13,
  output out_14
);

  not not_1 (out_9, in_1);
  not not_2 (out_11, in_4);
  not not_3 (out_13, in_6);
  not not_4 (out_10, in_3);
  not not_5 (out_12, in_5);
  not not_6 (out_14, in_7);
endmodule

// 74x08
module _74x08___Quad_2_input_AND (
  input  in_1,
  input  VCC,
  input  in_3,
  input  in_4,
  input  in_5,
  input  in_6,
  input  in_7,
  input  in_8,
  input  in_9,
  input  GND,
  output out_11,
  output out_12,
  output out_13,
  output out_14
);

  and and_1 (out_11, in_3, in_1);
  and and_2 (out_13, in_7, in_6);
  and and_3 (out_12, in_4, in_5);
  and and_4 (out_14, in_8, in_9);
endmodule

// 74x32
module _74x32___Quad_2_input_OR (
  input  in_1,
  input  VCC,
  input  in_3,
  input  in_4,
  input  in_5,
  input  in_6,
  input  in_7,
  input  in_8,
  input  in_9,
  input  GND,
  output out_11,
  output out_12,
  output out_13,
  output out_14
);

  or or_1 (out_11, in_3, in_1);
  or or_2 (out_13, in_7, in_6);
  or or_3 (out_12, in_4, in_5);
  or or_4 (out_14, in_8, in_9);
endmodule
