// Logisim project RiscvOnBusCpu-1.circ as structural Verilog: 15 circuits, main circuit ◇指令译码器
module \单总线CPU_微程序  (
  output [21:0] \控制总线 
);

  wire and_1_out, CLK, comparator_1_eq, comparator_2_eq, equal, not_1_out, risc_v_alu_1_equal, RST;
  wire [4:0] registerfile_1_p6, \微地址_状态 ;
  wire [11:0] Clks, \指令数 ;
  wire [31:0] AR_q, bit_extender_1_out, bit_extender_2_out, bit_extender_3_out, controlled_buffer_1_out,
       controlled_buffer_3_out, DR_q, IR, PC_q, ram_1_data, registerfile_1_p7, risc_v_alu_1_result,
       shifter_1_out, subtractor_1_out, X_q, Z_q, \内总线 ;

  // Probe on Clks
  Register #(.width(32), .trigger("rising"), .Select("low")) AR (
    .D(\内总线 ), .en(\控制总线 [12]), .Q(AR_q), .clk(CLK));  // open: clr
  // Probe on controlled_buffer_3_out
  // RiscV_Probe riscv_probe_1: pin names not known; wires that end beside it: IR
  Register #(.width(32), .trigger("rising"), .Select("low")) X (
    .D(\内总线 ), .en(\控制总线 [9]), .Q(X_q), .clk(CLK));  // open: clr
  // Probe on \指令数 
  RAM #(.addrWidth(10), .dataWidth(32), .bus("separate"), .Select("high")) ram_1 (
    .addr(AR_q[11:2]), .din(controlled_buffer_3_out), .data(ram_1_data), .str(\控制总线 [0]), .clk(CLK),
    .ld(\控制总线 [1]));  // open: sel, clr
  RISC_V_ALU risc_v_alu_1 (
    .X(X_q), .Y(\内总线 ), .Equal(risc_v_alu_1_equal), .Result(risc_v_alu_1_result), .ADD(\控制总线 [4]),
    .ADD4(\控制总线 [3]), .SLT(\控制总线 [2]));  // open: SUB
  assign controlled_buffer_1_out = \控制总线 [10] ? \内总线  : 32'bz;  // Controlled_Buffer controlled_buffer_1
  assign controlled_buffer_1_out = \控制总线 [11] ? ram_1_data : 32'bz;  // Controlled_Buffer controlled_buffer_2
  assign controlled_buffer_3_out = \控制总线 [14] ? DR_q : 32'bz;  // Controlled_Buffer controlled_buffer_3
  // Probe on \内总线 
  Register #(.width(32), .trigger("rising"), .Select("low")) PC (
    .D(\内总线 ), .en(\控制总线 [13]), .Q(PC_q), .clk(CLK), .clr(RST));
  Register #(.width(32), .trigger("rising"), .Select("low")) DR (
    .D(controlled_buffer_1_out), .Q(DR_q), .clk(CLK));  // open: en, clr
  Register #(.width(1), .trigger("rising"), .Select("low")) PSW (
    .D(risc_v_alu_1_equal), .en(\控制总线 [6]), .Q(equal), .clk(CLK));  // open: clr
  Register #(.width(32), .trigger("rising"), .Select("low")) Z (
    .D(risc_v_alu_1_result), .Q(Z_q), .clk(CLK));  // open: en, clr
  assign \内总线  = \控制总线 [21] ? PC_q : 32'bz;  // Controlled_Buffer controlled_buffer_4
  assign \内总线  = \控制总线 [20] ? DR_q : 32'bz;  // Controlled_Buffer controlled_buffer_5
  assign \内总线  = \控制总线 [19] ? Z_q : 32'bz;  // Controlled_Buffer controlled_buffer_6
  Register #(.width(32), .trigger("rising"), .Select("low")) u_IR (
    .D(\内总线 ), .en(\控制总线 [7]), .Q(IR), .clk(CLK));  // open: clr
  \微程序控制器  \u_微程序控制器_1  (.CLK(CLK), .EQUAL(equal), .mAddr(\微地址_状态 ), .\控制总线 (\控制总线 ), .\指令字 (IR));
  Comparator #(.width(32), .mode("twosComplement")) comparator_1 (
    .a(IR), .b(32'h63), .eq(comparator_1_eq));  // open: gt, lt
  Clock #(.highDuration(1), .lowDuration(1)) clock_1 (.out(CLK));
  // Probe on \微地址_状态 
  // RegisterFile registerfile_1: pin names not known; wires that end beside it: \内总线 , CLK, \控制总线 [8], IR, IR[11:7], registerfile_1_p6, registerfile_1_p7
  not not_1 (not_1_out, comparator_1_eq);
  Counter #(.width(12), .max('hfff), .ongoal("wrap"), .trigger("rising"), .behavior("new")) counter_1 (
    .count(not_1_out), .Q(Clks), .clk(CLK));  // open: load, D, carry, clr, preset, down
  assign bit_extender_1_out = {{20{IR[31]}}, {IR[31], IR[7], IR[30:25], IR[11:8]}};  // Bit_Extender bit_extender_1
  assign \内总线  = \控制总线 [18] ? registerfile_1_p7 : 32'bz;  // Controlled_Buffer controlled_buffer_7
  Multiplexer #(.select(1), .width(5), .disabled("Z"), .enable("false")) multiplexer_1 (
    .in0(IR[19:15]), .in1(IR[24:20]), .out(registerfile_1_p6), .sel(\控制总线 [5]));
  assign bit_extender_2_out = {{20{IR[31]}}, {IR[31:25], IR[11:7]}};  // Bit_Extender bit_extender_2
  assign bit_extender_3_out = {{20{IR[31]}}, IR[31:20]};  // Bit_Extender bit_extender_3
  Shifter #(.width(32), .shift("ll")) shifter_1 (.in(bit_extender_1_out), .\dist (5'b00001), .out(shifter_1_out));
  Subtractor #(.width(32)) subtractor_1 (.a(shifter_1_out), .b(32'h4), .out(subtractor_1_out));  // open: bin, bout
  and and_1 (and_1_out, not_1_out, comparator_2_eq);
  Comparator #(.width(5), .mode("twosComplement")) comparator_2 (
    .a(5'b00011), .b(\微地址_状态 ), .eq(comparator_2_eq));  // open: gt, lt
  assign \内总线  = \控制总线 [17] ? bit_extender_3_out : 32'bz;  // Controlled_Buffer controlled_buffer_8
  assign \内总线  = \控制总线 [15] ? subtractor_1_out : 32'bz;  // Controlled_Buffer controlled_buffer_9
  Counter #(.width(12), .max('hfff), .ongoal("wrap"), .trigger("rising"), .behavior("old")) counter_2 (
    .count(and_1_out), .Q(\指令数 ), .clk(CLK));  // open: load, D, carry, clr, preset
  assign \内总线  = \控制总线 [16] ? bit_extender_2_out : 32'bz;  // Controlled_Buffer controlled_buffer_10

  // Other names for the same wires on the sheet: rd[4:0] = IR[11:7]; rs1[4:0] = IR[19:15]; rs2[4:0] = IR[24:20];
  //   Write = \控制总线 [0]; READ = \控制总线 [1]; Slt = \控制总线 [2]; Add4 = \控制总线 [3]; Add = \控制总线 [4]; rs1_2 = \控制总线 [5];
  //   PSWin = \控制总线 [6]; IRin = \控制总线 [7]; Rin = \控制总线 [8]; Xin = \控制总线 [9]; DRin = \控制总线 [10]; DREin = \控制总线 [11];
  //   ARin = \控制总线 [12]; PCin = \控制总线 [13]; DREout = \控制总线 [14]; IR_B_out = \控制总线 [15]; IR_S_out = \控制总线 [16];
  //   IR_I_out = \控制总线 [17]; Rout = \控制总线 [18]; Zout = \控制总线 [19]; DRout = \控制总线 [20]; PCout = \控制总线 [21]

  // Notes on the sheet:
  //   单总线 RISC-V 现代时序
  //   RAM
  //   外总线
  //   内总线
  //   B_imm12
endmodule

// Decoder
module \指令译码器  (
  input  [31:0] IR,
  output LW,
  output SW,
  output BEQ,
  output ADDI,
  output SLT,
  output OtherInstr
);

  wire comparator_1_eq;

  Comparator #(.width(8), .mode("twosComplement")) comparator_1 (
    .a({IR[14:12], IR[6:2]}), .b(8'hc), .eq(comparator_1_eq));  // open: gt, lt
  nor nor_1 (OtherInstr, BEQ, SW, LW, ADDI, SLT);

  // Other names for the same wires on the sheet: FUNCT7[6:0] = IR[31:25]; OP[4:0] = IR[6:2];
  //   OP_Funct3[7:0] = {IR[14:12], IR[6:2]}; FUNCT3[2:0] = IR[14:12]
endmodule

module \微程序控制器  (
  input  EQUAL,
  input  [31:0] \指令字 ,
  input  CLK,
  output [4:0] mAddr,
  output [21:0] \控制总线 
);

  wire ADDI, BEQ, LW, Other, P0, P1, P2, SLT, SW;
  wire [1:0] \条件判别测试逻辑_1_s0 ;
  wire [4:0] multiplexer_1_out, rom_1_data, undriven, undriven_2, undriven_3, \微程序入口查找逻辑_1_s0 ;

  \微程序入口查找逻辑  \u_微程序入口查找逻辑_1  (
    .LW(LW), .SW(SW), .BEQ(BEQ), .SLT(SLT), .ADDI(ADDI), .S4(\微程序入口查找逻辑_1_s0 [4]), .S3(\微程序入口查找逻辑_1_s0 [3]),
    .S2(\微程序入口查找逻辑_1_s0 [2]), .S1(\微程序入口查找逻辑_1_s0 [1]), .S0(\微程序入口查找逻辑_1_s0 [0]));
  // Probe on \微程序入口查找逻辑_1_s0 
  \条件判别测试逻辑  \u_条件判别测试逻辑_1  (.P0(P0), .P1(P1), .equal(EQUAL), .S1(\条件判别测试逻辑_1_s0 [1]), .S0(\条件判别测试逻辑_1_s0 [0]));
  Multiplexer #(.select(2), .width(5), .disabled("Z"), .enable("false")) multiplexer_1 (
    .in0(undriven_2), .in1(undriven), .in2(undriven_3), .out(multiplexer_1_out));  // open: in3, sel
  Register #(.width(5), .trigger("falling"), .Select("low")) register_1 (
    .D(multiplexer_1_out), .Q(mAddr), .clk(CLK));  // open: en, clr
  // Probe on mAddr
  \指令译码器  \u_指令译码器_1  (.IR(\指令字 ), .LW(LW), .SW(SW), .BEQ(BEQ), .ADDI(ADDI), .SLT(SLT), .OtherInstr(Other));
  ROM #(.addrWidth(5), .dataWidth(30), .Select("high")) rom_1 (.addr(mAddr), .data({\控制总线 , P0, P1, P2, rom_1_data}));

  // Notes on the sheet:
  //   不要改变此引脚区域内容，也不要改变封装形式
  //   地址转移逻辑
  //   入口地址
  //   beq分支
  //   下址字段
  //   输入输出引脚
  //   μAR
  //   时钟是上跳沿还是下跳沿有效？
  //   微程序控制器（下址字段法）
  //   微地址
  //   控制存储器
  //   指令译码器
  //   控制字段
  //   指令译码信号
  //   微指令
  //   指令译码逻辑ID
  //   判断逻辑
endmodule

module \微程序入口查找逻辑  (
  input  LW,
  input  SW,
  input  BEQ,
  input  SLT,
  input  ADDI,
  output S4,
  output S3,
  output S2,
  output S1,
  output S0
);
endmodule

module \条件判别测试逻辑  (
  input  P0,
  input  P1,
  input  equal,
  output S1,
  output S0
);
endmodule

module \硬布线控制器  (
  input  EQUAL,
  input  [31:0] \指令字 ,
  input  CLK,
  output [4:0] statu,
  output [21:0] \控制总线 
);

  wire ADDI, BEQ, LW, Other, SLT, SW;
  wire [4:0] undriven;
  wire [7:0] rom_1_data;

  \硬布线状态机  \u_硬布线状态机_1  ();  // open: S4, S3, S2, S1, S0, LW, SW, BEQ, SLT, ADDI, EQUAL, N4, N3, N2, N1, N0
  // Probe on undriven
  Register #(.width(5), .trigger("falling"), .Select("low")) register_1 (
    .D(undriven), .Q(statu), .clk(CLK));  // open: en, clr
  \指令译码器  \u_指令译码器_1  (.IR(\指令字 ), .LW(LW), .SW(SW), .BEQ(BEQ), .ADDI(ADDI), .SLT(SLT), .OtherInstr(Other));
  ROM #(.addrWidth(5), .dataWidth(30), .Select("high")) rom_1 (.addr(statu), .data({\控制总线 , rom_1_data}));

  // Other names for the same wires on the sheet: status[4:0] = statu; Write = \控制总线 [0]; READ = \控制总线 [1];
  //   Slt_t = \控制总线 [2]; Add4 = \控制总线 [3]; Add = \控制总线 [4]; rs1_2 = \控制总线 [5]; PSWin = \控制总线 [6]; IRin = \控制总线 [7];
  //   Rin = \控制总线 [8]; Xin = \控制总线 [9]; DRin = \控制总线 [10]; DREin = \控制总线 [11]; ARin = \控制总线 [12]; PCin = \控制总线 [13];
  //   DREout = \控制总线 [14]; IR_B_out = \控制总线 [15]; IR_S_out = \控制总线 [16]; IR_I_out = \控制总线 [17]; Rout = \控制总线 [18];
  //   Zout = \控制总线 [19]; DRout = \控制总线 [20]; PCout = \控制总线 [21]

  // Notes on the sheet:
  //   不要改变此引脚区域内容，也不要改变封装形式
  //   输入输出引脚
  //   时钟是上跳沿还是下跳沿有效？
  //   状态寄存器
  //   指令译码器
  //   控制存储器
  //   指令译码信号
  //   控制字段
  //   微指令
  //   指令译码逻辑ID
endmodule

// 硬布线状态机
module \硬布线状态机  (
  input  S4,
  input  S3,
  input  S2,
  input  S1,
  input  S0,
  input  LW,
  input  SW,
  input  BEQ,
  input  SLT,
  input  ADDI,
  input  EQUAL,
  output N4,
  output N3,
  output N2,
  output N1,
  output N0
);
endmodule

module \单总线CPU_中断_微程序  (
  input  [1:0] EduInt,
  output [21:0] \控制总线 ,
  output [4:0] \EDU中断信号 
);

  wire _1_out, _2_out, and_1_out, CLK, comparator_1_eq, comparator_2_eq, equal, not_1_out,
       risc_v_alu_1_equal, RST, \中断控制器_1_intr , \中断控制器_1_ir1w , \中断控制器_1_ir2w , \中断请求 ;
  wire [1:0] \中断控制器_1_intno ;
  wire [4:0] registerfile_1_p6, \微地址_状态 ;
  wire [9:0] AR_q_2;
  wire [11:0] Clks, \指令数 ;
  wire [31:0] AR_q, bit_extender_1_out, bit_extender_2_out, bit_extender_3_out, controlled_buffer_1_out,
       controlled_buffer_3_out, DR_q, IR, PC_q, ram_1_data, registerfile_1_p7, risc_v_alu_1_result,
       shifter_1_out, subtractor_1_out, X_q, Z_q, \内总线 ;

  // Probe on Clks
  Register #(.width(32), .trigger("rising"), .Select("low")) AR (
    .D(\内总线 ), .en(\控制总线 [12]), .Q({AR_q[31:12], AR_q_2, AR_q[1:0]}), .clk(CLK));  // open: clr
  // Probe on controlled_buffer_3_out
  Register #(.width(32), .trigger("rising"), .Select("low")) X (
    .D(\内总线 ), .en(\控制总线 [9]), .Q(X_q), .clk(CLK));  // open: clr
  // RiscV_Probe riscv_probe_1: pin names not known; wires that end beside it: IR
  // Probe on \指令数 
  RAM #(.addrWidth(10), .dataWidth(32), .bus("separate"), .Select("high")) ram_1 (
    .addr(AR_q_2), .din(controlled_buffer_3_out), .data(ram_1_data), .str(\控制总线 [0]), .clk(CLK),
    .ld(\控制总线 [1]));  // open: sel, clr
  RISC_V_ALU risc_v_alu_1 (
    .X(X_q), .Y(\内总线 ), .Equal(risc_v_alu_1_equal), .Result(risc_v_alu_1_result), .ADD(\控制总线 [4]),
    .ADD4(\控制总线 [3]), .SLT(\控制总线 [2]));  // open: SUB
  assign controlled_buffer_1_out = \控制总线 [10] ? \内总线  : 32'bz;  // Controlled_Buffer controlled_buffer_1
  assign controlled_buffer_1_out = \控制总线 [11] ? ram_1_data : 32'bz;  // Controlled_Buffer controlled_buffer_2
  assign controlled_buffer_3_out = \控制总线 [14] ? DR_q : 32'bz;  // Controlled_Buffer controlled_buffer_3
  // Probe on \内总线 
  Register #(.width(32), .trigger("rising"), .Select("low")) PC (
    .D(\内总线 ), .en(\控制总线 [13]), .Q(PC_q), .clk(CLK), .clr(RST));
  Register #(.width(32), .trigger("rising"), .Select("low")) DR (
    .D(controlled_buffer_1_out), .Q(DR_q), .clk(CLK));  // open: en, clr
  Register #(.width(1), .trigger("rising"), .Select("low")) PSW (
    .D(risc_v_alu_1_equal), .en(\控制总线 [6]), .Q(equal), .clk(CLK));  // open: clr
  Register #(.width(32), .trigger("rising"), .Select("low")) Z (
    .D(risc_v_alu_1_result), .Q(Z_q), .clk(CLK));  // open: en, clr
  assign \内总线  = \控制总线 [21] ? PC_q : 32'bz;  // Controlled_Buffer controlled_buffer_4
  assign \内总线  = \控制总线 [20] ? DR_q : 32'bz;  // Controlled_Buffer controlled_buffer_5
  assign \内总线  = \控制总线 [19] ? Z_q : 32'bz;  // Controlled_Buffer controlled_buffer_6
  Register #(.width(32), .trigger("rising"), .Select("low")) u_IR (
    .D(\内总线 ), .en(\控制总线 [7]), .Q(IR), .clk(CLK));  // open: clr
  \微程序控制器_中断  \u_微程序控制器_中断_1  (
    .EQUAL(equal), .\指令字 (IR), .IntR(\中断请求 ), .CLK(CLK), .mAddr(\微地址_状态 ), .\控制总线 (\控制总线 ),
    .\中断控制信号 (\EDU中断信号 ));
  // Probe on \微地址_状态 
  Comparator #(.width(32), .mode("twosComplement")) comparator_1 (
    .a(IR), .b(32'h63), .eq(comparator_1_eq));  // open: gt, lt
  Clock #(.highDuration(1), .lowDuration(1)) clock_1 (.out(CLK));
  assign bit_extender_1_out = {{20{IR[31]}}, {IR[31], IR[7], IR[30:25], IR[11:8]}};  // Bit_Extender bit_extender_1
  // RegisterFile registerfile_1: pin names not known; wires that end beside it: \内总线 , CLK, \控制总线 [8], IR, IR[11:7], registerfile_1_p6, registerfile_1_p7
  Multiplexer #(.select(1), .width(5), .disabled("Z"), .enable("false")) multiplexer_1 (
    .in0(IR[19:15]), .in1(IR[24:20]), .out(registerfile_1_p6), .sel(\控制总线 [5]));
  not not_1 (not_1_out, comparator_1_eq);
  Counter #(.width(12), .max('hfff), .ongoal("wrap"), .trigger("rising"), .behavior("new")) counter_1 (
    .count(not_1_out), .Q(Clks), .clk(CLK));  // open: load, D, carry, clr, preset, down
  assign bit_extender_2_out = {{20{IR[31]}}, IR[31:20]};  // Bit_Extender bit_extender_2
  Shifter #(.width(32), .shift("ll")) shifter_1 (.in(bit_extender_1_out), .\dist (5'b00001), .out(shifter_1_out));
  assign \内总线  = \控制总线 [18] ? registerfile_1_p7 : 32'bz;  // Controlled_Buffer controlled_buffer_7
  Comparator #(.width(5), .mode("twosComplement")) comparator_2 (
    .a(5'b00011), .b(\微地址_状态 ), .eq(comparator_2_eq));  // open: gt, lt
  assign bit_extender_3_out = {{20{IR[31]}}, {IR[31:25], IR[11:7]}};  // Bit_Extender bit_extender_3
  Subtractor #(.width(32)) subtractor_1 (.a(shifter_1_out), .b(32'h4), .out(subtractor_1_out));  // open: bin, bout
  assign \内总线  = \控制总线 [15] ? subtractor_1_out : 32'bz;  // Controlled_Buffer controlled_buffer_8
  Counter #(.width(12), .max('hfff), .ongoal("wrap"), .trigger("rising"), .behavior("old")) counter_2 (
    .count(and_1_out), .Q(\指令数 ), .clk(CLK));  // open: load, D, carry, clr, preset
  and and_1 (and_1_out, not_1_out, comparator_2_eq);
  assign \内总线  = \控制总线 [17] ? bit_extender_2_out : 32'bz;  // Controlled_Buffer controlled_buffer_9
  assign \内总线  = \控制总线 [16] ? bit_extender_3_out : 32'bz;  // Controlled_Buffer controlled_buffer_10
  Button _1 (.out(_1_out));
  Button _2 (.out(_2_out));
  D_Flip_Flop #(.trigger("rising"), .Pre_Clr_Positions("LEGACY"), .NegatePresetClear("false"), .enable("true"), .NewFFLayout("false")) d_ff_1 (
    .preset(\EDU中断信号 [0]), .reset(\EDU中断信号 [1]));  // open: clk, D, Q, Qn, en
  LED #(.active("true")) _1_2 (.in(\中断控制器_1_ir1w ));
  LED #(.active("true")) _2_2 (.in(\中断控制器_1_ir2w ));
  \中断控制器  \u_中断控制器_1  (
    .CLK(CLK), .Key1(_1_out), .Key2(_2_out), .Clr(\EDU中断信号 [1]), .IR1W(\中断控制器_1_ir1w ),
    .IR2W(\中断控制器_1_ir2w ), .IntNo(\中断控制器_1_intno ), .IntR(\中断控制器_1_intr ), .EDU_TEST(EduInt));  // open: IR3W, Key3
  Register #(.width(32), .trigger("rising"), .Select("low")) mEPC (.clk(CLK));  // open: D, en, Q, clr

  // Other names for the same wires on the sheet: rd[4:0] = IR[11:7]; rs1[4:0] = IR[19:15]; rs2[4:0] = IR[24:20];
  //   中断控制信号[4:0] = \EDU中断信号 ; 关中断 = \EDU中断信号 [0]; 开中断 = \EDU中断信号 [1]; Addrout = \EDU中断信号 [2]; mEPCin = \EDU中断信号 [3];
  //   mEPCout = \EDU中断信号 [4]; Write = \控制总线 [0]; READ = \控制总线 [1]; Slt = \控制总线 [2]; Add4 = \控制总线 [3]; Add = \控制总线 [4];
  //   rs1_2 = \控制总线 [5]; PSWin = \控制总线 [6]; IRin = \控制总线 [7]; Rin = \控制总线 [8]; Xin = \控制总线 [9]; DRin = \控制总线 [10];
  //   DREin = \控制总线 [11]; ARin = \控制总线 [12]; PCin = \控制总线 [13]; DREout = \控制总线 [14]; IR_B_out = \控制总线 [15];
  //   IR_S_out = \控制总线 [16]; IR_I_out = \控制总线 [17]; Rout = \控制总线 [18]; Zout = \控制总线 [19]; DRout = \控制总线 [20];
  //   PCout = \控制总线 [21]

  // Notes on the sheet:
  //   单总线 RISC-V 现代时序+中断
  //   RAM
  //   外总线
  //   内总线
  //   B_imm12
  //   中断使能寄存器
  //   中断信号
  //   执行ERET时开中断，同时清除中断源
  //   中断逻辑
endmodule

module \微程序控制器_中断  (
  input  EQUAL,
  input  [31:0] \指令字 ,
  input  IntR,
  input  CLK,
  output [4:0] mAddr,
  output [21:0] \控制总线 ,
  output [4:0] \中断控制信号 
);

  wire ADDI, BEQ, ERET, LW, P0, P1, P2, SLT, SW;
  wire [4:0] adder_1_out, multiplexer_1_out, undriven, undriven_2, undriven_3, undriven_4, undriven_5,
       \微程序入口查找逻辑_中断_1_s0 ;

  \微程序入口查找逻辑_中断  \u_微程序入口查找逻辑_中断_1  (
    .LW(LW), .SW(SW), .BEQ(BEQ), .SLT(SLT), .ADDI(ADDI), .ERET(ERET), .S4(\微程序入口查找逻辑_中断_1_s0 [4]),
    .S3(\微程序入口查找逻辑_中断_1_s0 [3]), .S2(\微程序入口查找逻辑_中断_1_s0 [2]), .S1(\微程序入口查找逻辑_中断_1_s0 [1]),
    .S0(\微程序入口查找逻辑_中断_1_s0 [0]));
  // Probe on \微程序入口查找逻辑_中断_1_s0 
  \条件判别测试逻辑_中断  \u_条件判别测试逻辑_中断_1  (.P0(P0), .P1(P1), .P2(P2), .equal(EQUAL), .IntR(IntR));  // open: S2, S1, S0
  Multiplexer #(.select(3), .width(5), .disabled("Z"), .enable("false")) multiplexer_1 (
    .in0(undriven_4), .in1(undriven_3), .in2(undriven), .in3(undriven_2), .in4(undriven_5),
    .out(multiplexer_1_out));  // open: in5, in6, in7, sel
  // Probe on multiplexer_1_out
  Register #(.width(5), .trigger("falling"), .Select("low")) register_1 (
    .D(multiplexer_1_out), .Q(mAddr), .clk(CLK));  // open: en, clr
  Adder #(.width(5)) adder_1 (.a(5'b00001), .b(mAddr), .out(adder_1_out));  // open: cin, cout
  \指令译码器  \u_指令译码器_1  (.IR(\指令字 ), .LW(LW), .SW(SW), .BEQ(BEQ), .ADDI(ADDI), .SLT(SLT), .OtherInstr(ERET));
  ROM #(.addrWidth(5), .dataWidth(30), .Select("high")) rom_1 (.addr(mAddr), .data({\控制总线 , \中断控制信号 , P0, P1, P2}));

  // Notes on the sheet:
  //   不要改变此引脚区域内容，也不要改变封装形式
  //   地址转移逻辑
  //   根据指令进行微程序地址转移
  //   beq分支
  //   中断入口
  //   入口地址
  //   取指微程序入口
  //   顺序地址
  //   判别测试逻辑
  //   μAR
  //   支持中断的微程序控制器（计数器法）
  //   微地址
  //   指令译码器
  //   mAddr++
  //   控制存储器
  //   指令译码信号
  //   控制字段
  //   微指令
  //   指令译码逻辑ID
  //   判断逻辑
endmodule

// 入口查找
module \微程序入口查找逻辑_中断  (
  input  LW,
  input  SW,
  input  BEQ,
  input  SLT,
  input  ADDI,
  input  ERET,
  output S4,
  output S3,
  output S2,
  output S1,
  output S0
);
endmodule

// 判别
module \条件判别测试逻辑_中断  (
  input  P0,
  input  P1,
  input  P2,
  input  equal,
  input  IntR,
  output S2,
  output S1,
  output S0
);
endmodule

module \硬布线控制器_中断  (
  input  EQUAL,
  input  [31:0] \指令字 ,
  input  IntR,
  input  CLK,
  output [4:0] statu,
  output [21:0] \控制总线 ,
  output [4:0] \中断控制信号 
);

  wire ADDI, BEQ, ERET, LW, SLT, SW;
  wire [2:0] rom_1_data;
  wire [4:0] undriven;

  \硬布线状态机_中断  \u_硬布线状态机_中断_1  ();  // open: S4, S3, S2, S1, S0, LW, SW, BEQ, SLT, ADDI, URET, IR, EQUAL, N4, N3, N2, N1, N0
  // Probe on undriven
  Register #(.width(5), .trigger("falling"), .Select("low")) register_1 (
    .D(undriven), .Q(statu), .clk(CLK));  // open: en, clr
  // Probe on statu
  \指令译码器  \u_指令译码器_1  (.IR(\指令字 ), .LW(LW), .SW(SW), .BEQ(BEQ), .ADDI(ADDI), .SLT(SLT), .OtherInstr(ERET));
  ROM #(.addrWidth(5), .dataWidth(30), .Select("high")) rom_1 (.addr(statu), .data({\控制总线 , \中断控制信号 , rom_1_data}));

  // Other names for the same wires on the sheet: status[4:0] = statu

  // Notes on the sheet:
  //   不要改变此引脚区域内容，也不要改变封装形式
  //   根据指令进行微程序地址转移
  //   μAR
  //   支持中断的硬布线控制器
  //   指令译码器
  //   控制存储器
  //   指令译码信号
  //   控制字段
  //   微指令
  //   指令译码逻辑ID
endmodule

// 带中断硬布线状态机
module \硬布线状态机_中断  (
  input  S4,
  input  S3,
  input  S2,
  input  S1,
  input  S0,
  input  LW,
  input  SW,
  input  BEQ,
  input  SLT,
  input  ADDI,
  input  URET,
  input  IR,
  input  EQUAL,
  output N4,
  output N3,
  output N2,
  output N1,
  output N0
);
endmodule

// ALU
module RISC_V_ALU (
  input  ADD,
  input  ADD4,
  input  [31:0] X,
  input  [31:0] Y,
  input  SUB,
  input  SLT,
  output Equal,
  output [31:0] Result
);

  wire [0:0] comparator_1_lt;
  wire [1:0] priority_encoder_1_out;
  wire [31:0] adder_1_out, adder_2_out, subtractor_1_out;

  Pull_Resistor #(.pull(0)) pull_resistor_1 (.node(Y));
  Adder #(.width(32)) adder_1 (.a(X), .b(Y), .out(adder_1_out));  // open: cin, cout
  Adder #(.width(32)) adder_2 (.a(X), .b(32'h4), .out(adder_2_out));  // open: cin, cout
  Subtractor #(.width(32)) subtractor_1 (.a(X), .b(Y), .out(subtractor_1_out));  // open: bin, bout
  Comparator #(.width(32), .mode("twosComplement")) comparator_1 (
    .a(X), .b(Y), .eq(Equal), .lt(comparator_1_lt[0]));  // open: gt
  Priority_Encoder #(.select(2), .disabled("Z")) priority_encoder_1 (
    .in0(ADD), .in1(ADD4), .in2(SUB), .in3(SLT), .out(priority_encoder_1_out));  // open: gs, en_out, en_in
  Pull_Resistor #(.pull(0)) pull_resistor_2 (.node(priority_encoder_1_out));
  Multiplexer #(.select(2), .width(32), .disabled("Z"), .enable("false")) multiplexer_1 (
    .in0(adder_1_out), .in1(adder_2_out), .in2(subtractor_1_out), .in3({{31{1'b0}}, comparator_1_lt[0]}),
    .out(Result), .sel(priority_encoder_1_out));

  // Notes on the sheet:
  //   不要改变此引脚区域内容，也不要改变ALU封装形式
  //   输入引脚
  //   输出引脚
endmodule

// 中断控制器
module \中断控制器  (
  input  CLK,
  input  Key1,
  input  Key2,
  input  Key3,
  input  Clr,
  input  [1:0] EDU_TEST,
  output IR1W,
  output IR2W,
  output IR3W,
  output [1:0] IntNo,
  output IntR
);

  wire and_1_out, and_2_out, and_3_out, Clr0, Clr1, Clr2, Clr3, d_ff_1_q, d_ff_2_q, d_ff_3_q, IR1_q, IR2_q,
       IR3_q, or_1_out, or_3_out, or_6_out, or_7_out, or_8_out;

  or or_1 (or_1_out, Key1, EDU_TEST[0]);
  or or_2 (IR1W, IR1_q, d_ff_2_q);
  or or_3 (or_3_out, Key2, EDU_TEST[1]);
  or or_4 (IR2W, IR2_q, d_ff_3_q);
  D_Flip_Flop #(.trigger("rising"), .Pre_Clr_Positions("LEGACY"), .NegatePresetClear("false"), .enable("true"), .NewFFLayout("false")) d_ff_1 (
    .clk(Key3), .D(1'b1), .Q(d_ff_1_q), .reset(IR3_q));  // open: Qn, preset, en
  or or_5 (IR3W, IR3_q, d_ff_1_q);
  D_Flip_Flop #(.trigger("rising"), .Pre_Clr_Positions("LEGACY"), .NegatePresetClear("false"), .enable("true"), .NewFFLayout("false")) d_ff_2 (
    .clk(or_1_out), .D(1'b1), .Q(d_ff_2_q), .reset(IR1_q));  // open: Qn, preset, en
  D_Flip_Flop #(.trigger("rising"), .Pre_Clr_Positions("LEGACY"), .NegatePresetClear("false"), .enable("true"), .NewFFLayout("false")) d_ff_3 (
    .clk(or_3_out), .D(1'b1), .Q(d_ff_3_q), .reset(IR2_q));  // open: Qn, preset, en
  or or_6 (or_6_out, d_ff_2_q, IR1_q);
  and and_1 (and_1_out, or_6_out, ~Clr1);  // AND_Gate
  or or_7 (or_7_out, d_ff_3_q, IR2_q);
  and and_2 (and_2_out, or_7_out, ~Clr2);  // AND_Gate
  or or_8 (or_8_out, d_ff_1_q, IR3_q);
  and and_3 (and_3_out, or_8_out, ~Clr3);  // AND_Gate
  Pull_Resistor #(.pull(0)) pull_resistor_1 (.node(EDU_TEST));
  D_Flip_Flop #(.trigger("rising"), .Pre_Clr_Positions("LEGACY"), .NegatePresetClear("false"), .enable("true"), .NewFFLayout("false")) IR1 (
    .clk(CLK), .D(and_1_out), .Q(IR1_q));  // open: Qn, preset, en, reset
  D_Flip_Flop #(.trigger("rising"), .Pre_Clr_Positions("LEGACY"), .NegatePresetClear("false"), .enable("true"), .NewFFLayout("false")) IR2 (
    .clk(CLK), .D(and_2_out), .Q(IR2_q));  // open: Qn, preset, en, reset
  D_Flip_Flop #(.trigger("rising"), .Pre_Clr_Positions("LEGACY"), .NegatePresetClear("false"), .enable("true"), .NewFFLayout("false")) IR3 (
    .clk(CLK), .D(and_3_out), .Q(IR3_q));  // open: Qn, preset, en, reset
  Priority_Encoder #(.select(2), .disabled("Z")) priority_encoder_1 (
    .in1(IR1_q), .in2(IR2_q), .in3(IR3_q), .out(IntNo), .gs(IntR));  // open: in0, en_out, en_in
  Decoder #(.select(2), .tristate("false"), .disabled(0), .enable("true")) decoder_1 (
    .out0(Clr0), .out1(Clr1), .out2(Clr2), .out3(Clr3), .sel(IntNo), .en(Clr));

  // Other names for the same wires on the sheet: EDU_INT1 = EDU_TEST[0]; EDU_INT2 = EDU_TEST[1]

  // Notes on the sheet:
  //   中断等待
  //   中断等待
  //   中断等待
  //   中断信号采样参考电路
  //   Reset 
  //   Reset 
  //   Reset 
  //   中断优先编码器
endmodule
