// Logisim project RiscvOnBusCpu-3.circ as structural Verilog: 15 circuits, main circuit ◇硬布线控制器
module \单总线CPU_3级时序  (
  output [21:0] \控制总线 
);

  wire and_1_out, CLK, comparator_1_eq, equal, Mcal, Mex, Mif, Mint, not_1_out, risc_v_alu_1_equal, RST, T1,
       T2, T3, T4;
  wire [4:0] registerfile_1_p6;
  wire [11:0] Clks, \指令数 ;
  wire [31:0] AR_q, bit_extender_1_out, bit_extender_2_out, bit_extender_3_out, controlled_buffer_1_out,
       controlled_buffer_2_out, DR_q, IR, PC_q, ram_1_data, registerfile_1_p7, risc_v_alu_1_result,
       shifter_1_out, subtractor_1_out, X_q, Z_q, \内总线 ;

  LED #(.active("true")) led_1 (.in(Mcal));
  LED #(.active("true")) led_2 (.in(Mif));
  // Probe on Clks
  Register #(.width(32), .trigger("rising"), .Select("low")) AR (
    .D(\内总线 ), .en(\控制总线 [12]), .Q(AR_q), .clk(CLK));  // open: clr
  // Digital_Oscilloscope #(.nState(35), .frontlines("rising"), .showclock("true")) digital_oscilloscope_1: pin names not known; wires that end beside it: CLK, Mif, Mcal, Mex, T1, T2, T3, T4, \控制总线 [2]
  LED #(.active("true")) led_3 (.in(Mint));
  LED #(.active("true")) led_4 (.in(Mex));
  LED #(.active("true")) led_5 (.in(T1));
  // RiscV_Probe riscv_probe_1: pin names not known; wires that end beside it: IR
  // Probe on controlled_buffer_1_out
  Register #(.width(32), .trigger("rising"), .Select("low")) X (
    .D(\内总线 ), .en(\控制总线 [9]), .Q(X_q), .clk(CLK));  // open: clr
  LED #(.active("true")) led_6 (.in(T3));
  LED #(.active("true")) led_7 (.in(T2));
  // Probe on \指令数 
  LED #(.active("true")) led_8 (.in(T4));
  RAM #(.addrWidth(10), .dataWidth(32), .bus("separate"), .Select("high")) ram_1 (
    .addr(AR_q[11:2]), .din(controlled_buffer_1_out), .data(ram_1_data), .str(\控制总线 [0]), .clk(CLK),
    .ld(\控制总线 [1]));  // open: sel, clr
  assign controlled_buffer_1_out = \控制总线 [14] ? DR_q : 32'bz;  // Controlled_Buffer controlled_buffer_1
  RISC_V_ALU risc_v_alu_1 (
    .X(X_q), .Y(\内总线 ), .Equal(risc_v_alu_1_equal), .Result(risc_v_alu_1_result), .ADD(\控制总线 [4]),
    .ADD4(\控制总线 [3]), .SLT(\控制总线 [2]));  // open: SUB
  assign controlled_buffer_2_out = \控制总线 [10] ? \内总线  : 32'bz;  // Controlled_Buffer controlled_buffer_2
  assign controlled_buffer_2_out = \控制总线 [11] ? ram_1_data : 32'bz;  // Controlled_Buffer controlled_buffer_3
  // Probe on \内总线 
  assign \内总线  = \控制总线 [21] ? PC_q : 32'bz;  // Controlled_Buffer controlled_buffer_4
  Register #(.width(32), .trigger("rising"), .Select("low")) PC (
    .D(\内总线 ), .en(\控制总线 [13]), .Q(PC_q), .clk(CLK), .clr(RST));
  assign \内总线  = \控制总线 [20] ? DR_q : 32'bz;  // Controlled_Buffer controlled_buffer_5
  Register #(.width(32), .trigger("rising"), .Select("low")) DR (
    .D(controlled_buffer_2_out), .Q(DR_q), .clk(CLK));  // open: en, clr
  Register #(.width(1), .trigger("rising"), .Select("low")) PSW (
    .D(risc_v_alu_1_equal), .en(\控制总线 [6]), .Q(equal), .clk(CLK));  // open: clr
  assign \内总线  = \控制总线 [19] ? Z_q : 32'bz;  // Controlled_Buffer controlled_buffer_6
  Register #(.width(32), .trigger("rising"), .Select("low")) Z (
    .D(risc_v_alu_1_result), .Q(Z_q), .clk(CLK));  // open: en, clr
  Register #(.width(32), .trigger("rising"), .Select("low")) u_IR (
    .D(\内总线 ), .en(\控制总线 [7]), .Q(IR), .clk(CLK));  // open: clr
  \硬布线控制器  \u_硬布线控制器_1  (
    .\状态节拍信号 ({T4, T3, T2, T1, Mex, Mcal, Mif}), .CLK(CLK), .IR(IR), .\控制总线 (\控制总线 ), .EQUAL(equal));
  assign bit_extender_1_out = {{20{IR[31]}}, {IR[31], IR[7], IR[30:25], IR[11:8]}};  // Bit_Extender bit_extender_1
  // RegisterFile registerfile_1: pin names not known; wires that end beside it: \内总线 , CLK, \控制总线 [8], IR, IR[11:7], registerfile_1_p6, registerfile_1_p7
  Multiplexer #(.select(1), .width(5), .disabled("Z"), .enable("false")) multiplexer_1 (
    .in0(IR[19:15]), .in1(IR[24:20]), .out(registerfile_1_p6), .sel(\控制总线 [5]));
  assign bit_extender_2_out = {{20{IR[31]}}, IR[31:20]};  // Bit_Extender bit_extender_2
  Shifter #(.width(32), .shift("ll")) shifter_1 (.in(bit_extender_1_out), .\dist (5'b00001), .out(shifter_1_out));
  assign \内总线  = \控制总线 [18] ? registerfile_1_p7 : 32'bz;  // Controlled_Buffer controlled_buffer_7
  Comparator #(.width(32), .mode("twosComplement")) comparator_1 (
    .a(IR), .b(32'h63), .eq(comparator_1_eq));  // open: gt, lt
  not not_1 (not_1_out, comparator_1_eq);
  Clock #(.highDuration(1), .lowDuration(1)) clock_1 (.out(CLK));
  assign bit_extender_3_out = {{20{IR[31]}}, {IR[31:25], IR[11:7]}};  // Bit_Extender bit_extender_3
  Subtractor #(.width(32)) subtractor_1 (.a(shifter_1_out), .b(32'h4), .out(subtractor_1_out));  // open: bin, bout
  assign \内总线  = \控制总线 [15] ? subtractor_1_out : 32'bz;  // Controlled_Buffer controlled_buffer_8
  Counter #(.width(12), .max('hfff), .ongoal("wrap"), .trigger("falling"), .behavior("new")) counter_1 (
    .count(not_1_out), .Q(Clks), .clk(CLK));  // open: load, D, carry, clr, preset, down
  assign \内总线  = \控制总线 [17] ? bit_extender_2_out : 32'bz;  // Controlled_Buffer controlled_buffer_9
  and and_1 (and_1_out, not_1_out, Mif, T1);
  assign \内总线  = \控制总线 [16] ? bit_extender_3_out : 32'bz;  // Controlled_Buffer controlled_buffer_10
  Counter #(.width(12), .max('hfff), .ongoal("wrap"), .trigger("falling"), .behavior("old")) counter_2 (
    .count(and_1_out), .Q(\指令数 ), .clk(CLK));  // open: load, D, carry, clr, preset

  // Other names for the same wires on the sheet: rd[4:0] = IR[11:7]; rs1[4:0] = IR[19:15]; rs2[4:0] = IR[24:20];
  //   Write = \控制总线 [0]; READ = \控制总线 [1]; Slt = \控制总线 [2]; Add4 = \控制总线 [3]; Add = \控制总线 [4]; rs1_2 = \控制总线 [5];
  //   PSWin = \控制总线 [6]; IRin = \控制总线 [7]; Rin = \控制总线 [8]; Xin = \控制总线 [9]; DRin = \控制总线 [10]; DREin = \控制总线 [11];
  //   ARin = \控制总线 [12]; PCin = \控制总线 [13]; DREout = \控制总线 [14]; IR_B_out = \控制总线 [15]; IR_S_out = \控制总线 [16];
  //   IR_I_out = \控制总线 [17]; Rout = \控制总线 [18]; Zout = \控制总线 [19]; DRout = \控制总线 [20]; PCout = \控制总线 [21];
  //   状态节拍信号[6:0] = {T4, T3, T2, T1, Mex, Mcal, Mif}

  // Notes on the sheet:
  //   单总线 RISC-V 三级时序
  //   RAM
  //   外总线
  //   内总线
  //   三级时序
  //   B_imm12
endmodule

module \硬布线控制器  (
  input  CLK,
  input  [31:0] IR,
  input  EQUAL,
  output [6:0] \状态节拍信号 ,
  output [21:0] \控制总线 
);

  wire ADDI, BEQ, LW, Other;
  wire [3:0] undriven;
  wire [12:9] OCInput;

  \时序发生器状态机_定长指令周期  \u_时序发生器状态机_定长指令周期_1  ();  // open: S3, S2, S1, S0, N3, N2, N1, N0
  Register #(.width(4), .trigger("rising"), .Select("low")) register_1 ();  // open: D, en, Q, clk, clr
  \时序发生器状态机_变长指令周期  \u_时序发生器状态机_变长指令周期_1  ();  // open: LW, SW, BEQ, SLT, ADDI, S3, S2, S1, S0, N3, N2, N1, N0
  \时序发生器输出函数_定长指令周期  \u_时序发生器输出函数_定长指令周期_1  (
    .S3(undriven[3]), .S2(undriven[2]), .S1(undriven[1]), .S0(undriven[0]), .Mif(\状态节拍信号 [0]),
    .Mcal(\状态节拍信号 [1]), .Mex(\状态节拍信号 [2]), .T1(\状态节拍信号 [3]), .T2(\状态节拍信号 [4]), .T3(\状态节拍信号 [5]),
    .T4(\状态节拍信号 [6]));
  \时序发生器输出函数_变长指令周期  \u_时序发生器输出函数_变长指令周期_1  ();  // open: S3, S2, S1, S0, Mif, Mcal, Mex, T1, T2, T3, T4
  \指令译码器  \u_指令译码器_1  (
    .IR(IR), .LW(LW), .SW(OCInput[9]), .BEQ(BEQ), .ADDI(ADDI), .SLT(OCInput[12]), .OtherInstr(Other));
  \硬布线控制器组合逻辑单元  \u_硬布线控制器组合逻辑单元_1  (
    .SLT(OCInput[12]), .ADDI(ADDI), .LW(LW), .SW(OCInput[9]), .BEQ(BEQ), .Mif(\状态节拍信号 [0]),
    .Mcal(\状态节拍信号 [1]), .Mex(\状态节拍信号 [2]), .T1(\状态节拍信号 [3]), .T2(\状态节拍信号 [4]), .T3(\状态节拍信号 [5]),
    .T4(\状态节拍信号 [6]), .EQUAL(EQUAL), .Pcout(\控制总线 [21]), .DRout(\控制总线 [20]), .Zout(\控制总线 [19]),
    .Rout(\控制总线 [18]), .IRIout(\控制总线 [17]), .IRSout(\控制总线 [16]), .IRBout(\控制总线 [15]), .DREout(\控制总线 [14]),
    .Pcin(\控制总线 [13]), .ARin(\控制总线 [12]), .DREin(\控制总线 [11]), .DRin(\控制总线 [10]), .Xin(\控制总线 [9]),
    .Rin(\控制总线 [8]), .IRin(\控制总线 [7]), .PSWin(\控制总线 [6]), .rs12(\控制总线 [5]), .Add(\控制总线 [4]),
    .Add4(\控制总线 [3]), .Slt_2(\控制总线 [2]), .READ(\控制总线 [1]), .WRITE(\控制总线 [0]));

  // Other names for the same wires on the sheet: OCInput (some bits) = {ADDI, LW, BEQ, \状态节拍信号 [0], \状态节拍信号 [1], \状态节拍信号 [2], \状态节拍信号 [3], \状态节拍信号 [4], \状态节拍信号 [5], \状态节拍信号 [6], EQUAL};
  //   T4 = \状态节拍信号 [6]; T3 = \状态节拍信号 [5]; T2 = \状态节拍信号 [4]; T1 = \状态节拍信号 [3]; Mex = \状态节拍信号 [2]; Mcal = \状态节拍信号 [1];
  //   Mif = \状态节拍信号 [0]; SW = OCInput[9]; SLT = OCInput[12]; 指令字[31:0] = IR; Write = \控制总线 [0]; READ = \控制总线 [1];
  //   Slt_t = \控制总线 [2]; Add4 = \控制总线 [3]; Add = \控制总线 [4]; rs1_2 = \控制总线 [5]; PSWin = \控制总线 [6]; IRin = \控制总线 [7];
  //   Rin = \控制总线 [8]; Xin = \控制总线 [9]; DRin = \控制总线 [10]; DREin = \控制总线 [11]; ARin = \控制总线 [12]; PCin = \控制总线 [13];
  //   DREout = \控制总线 [14]; IR_B_out = \控制总线 [15]; IR_S_out = \控制总线 [16]; IR_I_out = \控制总线 [17]; Rout = \控制总线 [18];
  //   Zout = \控制总线 [19]; DRout = \控制总线 [20]; PCout = \控制总线 [21]

  // Notes on the sheet:
  //   不要改变此引脚区域内容，也不要改变封装形式
  //   指令译码信号
  //   状态寄存器
  //   状态寄存器应该下跳沿？
  //   FSM状态机
  //   输入输出引脚
  //   时序发生器TG
  //   指令译码器
  //   如发现控制信号有错可以直接查看具体哪位信号出错
  //   指令译码信号
  //   指令译码逻辑ID
  //   硬布线控制器组合逻辑单元
endmodule

// Decoder
module \指令译码器  (
  input  [31:0] IR,
  output LW,
  output SW,
  output BEQ,
  output ADDI,
  output SLT,
  output OtherInstr
);

  wire comparator_1_eq;

  Comparator #(.width(8), .mode("twosComplement")) comparator_1 (
    .a({IR[14:12], IR[6:2]}), .b(8'hc), .eq(comparator_1_eq));  // open: gt, lt
  nor nor_1 (OtherInstr, BEQ, SW, LW, ADDI, SLT);

  // Other names for the same wires on the sheet: FUNCT7[6:0] = IR[31:25]; OP[4:0] = IR[6:2];
  //   OP_Funct3[7:0] = {IR[14:12], IR[6:2]}; FUNCT3[2:0] = IR[14:12]

  // Notes on the sheet:
  //   请勿增删改引脚，否则可能引起子电路外观变化，无法自动测试
  //   将指令字IR转换成指令译码信息，每一个输出代表一条不同的指令
endmodule

// 状态机
module \时序发生器状态机_定长指令周期  (
  input  S3,
  input  S2,
  input  S1,
  input  S0,
  output N3,
  output N2,
  output N1,
  output N0
);
endmodule

// 输出函数
module \时序发生器输出函数_定长指令周期  (
  input  S3,
  input  S2,
  input  S1,
  input  S0,
  output Mif,
  output Mcal,
  output Mex,
  output T1,
  output T2,
  output T3,
  output T4
);
endmodule

// 状态机
module \时序发生器状态机_变长指令周期  (
  input  LW,
  input  SW,
  input  BEQ,
  input  SLT,
  input  ADDI,
  input  S3,
  input  S2,
  input  S1,
  input  S0,
  output N3,
  output N2,
  output N1,
  output N0
);
endmodule

// 输出函数
module \时序发生器输出函数_变长指令周期  (
  input  S3,
  input  S2,
  input  S1,
  input  S0,
  output Mif,
  output Mcal,
  output Mex,
  output T1,
  output T2,
  output T3,
  output T4
);
endmodule

// 硬布线控制器组合逻辑单元
module \硬布线控制器组合逻辑单元  (
  input  SLT,
  input  ADDI,
  input  LW,
  input  SW,
  input  BEQ,
  input  Mif,
  input  Mcal,
  input  Mex,
  input  T1,
  input  T2,
  input  T3,
  input  T4,
  input  EQUAL,
  output Pcout,
  output DRout,
  output Zout,
  output Rout,
  output IRIout,
  output IRSout,
  output IRBout,
  output DREout,
  output Pcin,
  output ARin,
  output DREin,
  output DRin,
  output Xin,
  output Rin,
  output IRin,
  output PSWin,
  output rs12,
  output Add,
  output Add4,
  output Slt_2,
  output READ,
  output WRITE
);
endmodule

module \单总线CPU_中断_3级时序  (
  input  [1:0] EduInt,
  output [21:0] \控制总线 ,
  output [4:0] \EDU中断信号 
);

  wire _1_out, _2_out, and_1_out, CLK, comparator_1_eq, equal, Mcal, Mex, Mif, Mint, not_1_out,
       risc_v_alu_1_equal, RST, T1, T2, T3, T4, \中断控制器_1_ir1w , \中断控制器_1_ir2w , \中断请求 ;
  wire [4:0] registerfile_1_p8;
  wire [9:0] AR_q_2;
  wire [11:0] Clks, \指令数 ;
  wire [31:0] AR_q, bit_extender_1_out, bit_extender_2_out, bit_extender_3_out, controlled_buffer_1_out,
       controlled_buffer_3_out, DR_q, IR, PC_q, ram_1_data, registerfile_1_p9, risc_v_alu_1_result,
       shifter_1_out, subtractor_1_out, X_q, Z_q, \内总线 ;

  // Probe on Clks
  Register #(.width(32), .trigger("rising"), .Select("low")) AR (
    .D(\内总线 ), .en(\控制总线 [12]), .Q({AR_q[31:12], AR_q_2, AR_q[1:0]}), .clk(CLK));  // open: clr
  // Probe on controlled_buffer_3_out
  Register #(.width(32), .trigger("rising"), .Select("low")) X (
    .D(\内总线 ), .en(\控制总线 [9]), .Q(X_q), .clk(CLK));  // open: clr
  // RiscV_Probe riscv_probe_1: pin names not known; wires that end beside it: IR
  // Probe on \指令数 
  RAM #(.addrWidth(10), .dataWidth(32), .bus("separate"), .Select("high")) ram_1 (
    .addr(AR_q_2), .din(controlled_buffer_3_out), .data(ram_1_data), .str(\控制总线 [0]), .clk(CLK),
    .ld(\控制总线 [1]));  // open: sel, clr
  RISC_V_ALU risc_v_alu_1 (
    .X(X_q), .Y(\内总线 ), .Equal(risc_v_alu_1_equal), .Result(risc_v_alu_1_result), .ADD(\控制总线 [4]),
    .ADD4(\控制总线 [3]), .SLT(\控制总线 [2]));  // open: SUB
  assign controlled_buffer_1_out = \控制总线 [10] ? \内总线  : 32'bz;  // Controlled_Buffer controlled_buffer_1
  assign controlled_buffer_1_out = \控制总线 [11] ? ram_1_data : 32'bz;  // Controlled_Buffer controlled_buffer_2
  assign controlled_buffer_3_out = \控制总线 [14] ? DR_q : 32'bz;  // Controlled_Buffer controlled_buffer_3
  // Probe on \内总线 
  Register #(.width(32), .trigger("rising"), .Select("low")) PC (
    .D(\内总线 ), .en(\控制总线 [13]), .Q(PC_q), .clk(CLK), .clr(RST));
  Register #(.width(32), .trigger("rising"), .Select("low")) DR (
    .D(controlled_buffer_1_out), .Q(DR_q), .clk(CLK));  // open: en, clr
  Register #(.width(1), .trigger("rising"), .Select("low")) PSW (
    .D(risc_v_alu_1_equal), .en(\控制总线 [6]), .Q(equal), .clk(CLK));  // open: clr
  Register #(.width(32), .trigger("rising"), .Select("low")) Z (
    .D(risc_v_alu_1_result), .Q(Z_q), .clk(CLK));  // open: en, clr
  assign \内总线  = \控制总线 [21] ? PC_q : 32'bz;  // Controlled_Buffer controlled_buffer_4
  assign \内总线  = \控制总线 [20] ? DR_q : 32'bz;  // Controlled_Buffer controlled_buffer_5
  assign \内总线  = \控制总线 [19] ? Z_q : 32'bz;  // Controlled_Buffer controlled_buffer_6
  Register #(.width(32), .trigger("rising"), .Select("low")) u_IR (
    .D(\内总线 ), .en(\控制总线 [7]), .Q(IR), .clk(CLK));  // open: clr
  \硬布线控制器_中断  \u_硬布线控制器_中断_1  (
    .CLK(CLK), .IR(IR), .EQUAL(equal), .M_T({Mif, Mcal, Mex, Mint, T1, T2, T3, T4}), .\控制总线 (\控制总线 ),
    .\中断控制信号 (\EDU中断信号 ), .IntR(\中断请求 ));
  assign bit_extender_1_out = {{20{IR[31]}}, {IR[31], IR[7], IR[30:25], IR[11:8]}};  // Bit_Extender bit_extender_1
  // RegisterFile registerfile_1: pin names not known; wires that end beside it: \控制总线 [20], \内总线 , CLK, \控制总线 [8], IR, IR[11:7], \控制总线 [15], registerfile_1_p8, registerfile_1_p9
  Multiplexer #(.select(1), .width(5), .disabled("Z"), .enable("false")) multiplexer_1 (
    .in0(IR[19:15]), .in1(IR[24:20]), .out(registerfile_1_p8), .sel(\控制总线 [5]));
  assign bit_extender_2_out = {{20{IR[31]}}, IR[31:20]};  // Bit_Extender bit_extender_2
  Shifter #(.width(32), .shift("ll")) shifter_1 (.in(bit_extender_1_out), .\dist (5'b00001), .out(shifter_1_out));
  assign \内总线  = \控制总线 [18] ? registerfile_1_p9 : 32'bz;  // Controlled_Buffer controlled_buffer_7
  assign bit_extender_3_out = {{20{IR[31]}}, {IR[31:25], IR[11:7]}};  // Bit_Extender bit_extender_3
  Subtractor #(.width(32)) subtractor_1 (.a(shifter_1_out), .b(32'h4), .out(subtractor_1_out));  // open: bin, bout
  assign \内总线  = \控制总线 [15] ? subtractor_1_out : 32'bz;  // Controlled_Buffer controlled_buffer_8
  assign \内总线  = \控制总线 [17] ? bit_extender_2_out : 32'bz;  // Controlled_Buffer controlled_buffer_9
  assign \内总线  = \控制总线 [16] ? bit_extender_3_out : 32'bz;  // Controlled_Buffer controlled_buffer_10
  Button _1 (.out(_1_out));
  Button _2 (.out(_2_out));
  not not_1 (not_1_out, comparator_1_eq);
  Comparator #(.width(32), .mode("twosComplement")) comparator_1 (
    .a(IR), .b(32'h63), .eq(comparator_1_eq));  // open: gt, lt
  Clock #(.highDuration(1), .lowDuration(1)) clock_1 (.out(CLK));
  D_Flip_Flop #(.trigger("rising"), .Pre_Clr_Positions("LEGACY"), .NegatePresetClear("false"), .enable("true"), .NewFFLayout("false")) d_ff_1 (
    .preset(\EDU中断信号 [0]), .reset(\EDU中断信号 [1]));  // open: clk, D, Q, Qn, en
  LED #(.active("true")) _1_2 (.in(\中断控制器_1_ir1w ));
  LED #(.active("true")) _2_2 (.in(\中断控制器_1_ir2w ));
  \中断控制器  \u_中断控制器_1  (
    .CLK(CLK), .Key1(_1_out), .Key2(_2_out), .Clr(\EDU中断信号 [1]), .IR1W(\中断控制器_1_ir1w ),
    .IR2W(\中断控制器_1_ir2w ), .EDU_TEST(EduInt));  // open: IR3W, IntNo, IntR, Key3
  Counter #(.width(12), .max('hfff), .ongoal("wrap"), .trigger("falling"), .behavior("new")) counter_1 (
    .count(not_1_out), .Q(Clks), .clk(CLK));  // open: load, D, carry, clr, preset, down
  Register #(.width(32), .trigger("rising"), .Select("low")) mEPC (.clk(CLK));  // open: D, en, Q, clr
  Counter #(.width(12), .max('hfff), .ongoal("wrap"), .trigger("falling"), .behavior("old")) counter_2 (
    .count(and_1_out), .Q(\指令数 ), .clk(CLK));  // open: load, D, carry, clr, preset
  and and_1 (and_1_out, not_1_out, Mif, T1);

  // Other names for the same wires on the sheet: rd[4:0] = IR[11:7]; rs1[4:0] = IR[19:15]; rs2[4:0] = IR[24:20];
  //   中断控制信号[4:0] = \EDU中断信号 ; 关中断 = \EDU中断信号 [0]; 开中断 = \EDU中断信号 [1]; Addrout = \EDU中断信号 [2]; mEPCin = \EDU中断信号 [3];
  //   mEPCout = \EDU中断信号 [4]; Write = \控制总线 [0]; READ = \控制总线 [1]; Slt = \控制总线 [2]; Add4 = \控制总线 [3]; Add = \控制总线 [4];
  //   rs1_2 = \控制总线 [5]; PSWin = \控制总线 [6]; IRin = \控制总线 [7]; Rin = \控制总线 [8]; Xin = \控制总线 [9]; DRin = \控制总线 [10];
  //   DREin = \控制总线 [11]; ARin = \控制总线 [12]; PCin = \控制总线 [13]; DREout = \控制总线 [14]; IR_B_out = \控制总线 [15];
  //   IR_S_out = \控制总线 [16]; IR_I_out = \控制总线 [17]; Rout = \控制总线 [18]; Zout = \控制总线 [19]; DRout = \控制总线 [20];
  //   PCout = \控制总线 [21]; 状态节拍信号[7:0] = {Mif, Mcal, Mex, Mint, T1, T2, T3, T4}

  // Notes on the sheet:
  //   单总线 RISC-V 三级时序+中断
  //   RAM
  //   外总线
  //   内总线
  //   三级时序
  //   B_imm12
  //   中断使能寄存器
  //   中断信号
  //   执行MERET时开中断，同时清除中断源
  //   mEPC用于保存断点
  //   中断逻辑
endmodule

module \硬布线控制器_中断  (
  input  CLK,
  input  [31:0] IR,
  input  EQUAL,
  input  IntR,
  output [7:0] M_T,
  output [21:0] \控制总线 ,
  output [4:0] \中断控制信号 
);

  wire ADDI, BEQ, ERET, LW, PCin1, PCout1, \中断信号控制器_pcin , \中断信号控制器_pcout ;
  wire [3:0] undriven;
  wire [12:9] OCInput;

  Register #(.width(4), .trigger("rising"), .Select("low")) register_1 ();  // open: D, en, Q, clk, clr
  \时序发生器状态机_中断  \u_时序发生器状态机_中断_1  (.IntR(IntR));  // open: ERET, LW, SW, BEQ, SLT, ADDI, S3, S2, S1, S0, N3, N2, N1, N0
  \时序发生器输出函数_中断  \u_时序发生器输出函数_中断_1  (
    .S3(undriven[3]), .S2(undriven[2]), .S1(undriven[1]), .S0(undriven[0]), .Mif(M_T[7]), .Mcal(M_T[6]),
    .Mex(M_T[5]), .Mint(M_T[4]), .T1(M_T[3]), .T2(M_T[2]), .T3(M_T[1]), .T4(M_T[0]));
  \中断信号控制器  \u_中断信号控制器  (
    .ERET(ERET), .Mex(M_T[5]), .Mint(M_T[4]), .T1(M_T[3]), .T2(M_T[2]), .Pcout(\中断信号控制器_pcout ),
    .PCin(\中断信号控制器_pcin ), .mEPCout(\中断控制信号 [4]), .mEPCin(\中断控制信号 [3]), .Addrout(\中断控制信号 [2]),
    .STI(\中断控制信号 [1]), .CLI(\中断控制信号 [0]));
  \指令译码器  \u_指令译码器_1  (.IR(IR), .LW(LW), .SW(OCInput[9]), .BEQ(BEQ), .ADDI(ADDI), .SLT(OCInput[12]), .OtherInstr(ERET));
  or or_1 (\控制总线 [21], PCout1, \中断信号控制器_pcout );
  or or_2 (\控制总线 [13], \中断信号控制器_pcin , PCin1);
  \硬布线控制器组合逻辑单元  \u_硬布线控制器组合逻辑单元_1  (
    .SLT(OCInput[12]), .ADDI(ADDI), .LW(LW), .SW(OCInput[9]), .BEQ(BEQ), .Mif(M_T[7]), .Mcal(M_T[6]),
    .Mex(M_T[5]), .T1(M_T[3]), .T2(M_T[2]), .T3(M_T[1]), .T4(M_T[0]), .EQUAL(EQUAL), .Pcout(PCout1),
    .DRout(\控制总线 [20]), .Zout(\控制总线 [19]), .Rout(\控制总线 [18]), .IRIout(\控制总线 [17]), .IRSout(\控制总线 [16]),
    .IRBout(\控制总线 [15]), .DREout(\控制总线 [14]), .Pcin(PCin1), .ARin(\控制总线 [12]), .DREin(\控制总线 [11]),
    .DRin(\控制总线 [10]), .Xin(\控制总线 [9]), .Rin(\控制总线 [8]), .IRin(\控制总线 [7]), .PSWin(\控制总线 [6]),
    .rs12(\控制总线 [5]), .Add(\控制总线 [4]), .Add4(\控制总线 [3]), .Slt_2(\控制总线 [2]), .READ(\控制总线 [1]),
    .WRITE(\控制总线 [0]));

  // Other names for the same wires on the sheet: Mint = M_T[4];
  //   OCInput (some bits) = {ADDI, LW, BEQ, M_T[7:5], M_T[3:0], EQUAL}; T4 = M_T[0]; T3 = M_T[1]; T2 = M_T[2];
  //   T1 = M_T[3]; Mex = M_T[5]; Mcal = M_T[6]; Mif = M_T[7]; SW = OCInput[9]; SLT = OCInput[12]; 指令字[31:0] = IR;
  //   PCin = \控制总线 [13]; PCout = \控制总线 [21]

  // Notes on the sheet:
  //   指令译码信号
  //   中断控制相关信号生成逻辑
  //   不要改变此引脚区域内容，也不要改变封装形式
  //   状态寄存器
  //   状态寄存器应该下跳沿？
  //   FSM状态机
  //   输入输出引脚
  //   时序产生器TG
  //   指令译码器
  //   注意：IntSignals中的信号和上面的硬布线控制器组合逻辑单元无关，相关信号要合并处理
  //   指令译码信号
  //   指令译码逻辑ID
  //   操作控制器OC
endmodule

// 状态机
module \时序发生器状态机_中断  (
  input  ERET,
  input  LW,
  input  SW,
  input  BEQ,
  input  SLT,
  input  ADDI,
  input  IntR,
  input  S3,
  input  S2,
  input  S1,
  input  S0,
  output N3,
  output N2,
  output N1,
  output N0
);
endmodule

// 输出函数
module \时序发生器输出函数_中断  (
  input  S3,
  input  S2,
  input  S1,
  input  S0,
  output Mif,
  output Mcal,
  output Mex,
  output Mint,
  output T1,
  output T2,
  output T3,
  output T4
);
endmodule

// 中断相关
module \中断信号控制器  (
  input  ERET,
  input  Mex,
  input  Mint,
  input  T1,
  input  T2,
  output Pcout,
  output PCin,
  output mEPCout,
  output mEPCin,
  output Addrout,
  output STI,
  output CLI
);
endmodule

// ALU
module RISC_V_ALU (
  input  ADD,
  input  ADD4,
  input  [31:0] X,
  input  [31:0] Y,
  input  SUB,
  input  SLT,
  output Equal,
  output [31:0] Result
);

  wire [0:0] comparator_1_lt;
  wire [1:0] priority_encoder_1_out;
  wire [31:0] adder_1_out, adder_2_out, subtractor_1_out;

  Pull_Resistor #(.pull(0)) pull_resistor_1 (.node(Y));
  Adder #(.width(32)) adder_1 (.a(X), .b(Y), .out(adder_1_out));  // open: cin, cout
  Adder #(.width(32)) adder_2 (.a(X), .b(32'h4), .out(adder_2_out));  // open: cin, cout
  Subtractor #(.width(32)) subtractor_1 (.a(X), .b(Y), .out(subtractor_1_out));  // open: bin, bout
  Comparator #(.width(32), .mode("twosComplement")) comparator_1 (
    .a(X), .b(Y), .eq(Equal), .lt(comparator_1_lt[0]));  // open: gt
  Priority_Encoder #(.select(2), .disabled("Z")) priority_encoder_1 (
    .in0(ADD), .in1(ADD4), .in2(SUB), .in3(SLT), .out(priority_encoder_1_out));  // open: gs, en_out, en_in
  Pull_Resistor #(.pull(0)) pull_resistor_2 (.node(priority_encoder_1_out));
  Multiplexer #(.select(2), .width(32), .disabled("Z"), .enable("false")) multiplexer_1 (
    .in0(adder_1_out), .in1(adder_2_out), .in2(subtractor_1_out), .in3({{31{1'b0}}, comparator_1_lt[0]}),
    .out(Result), .sel(priority_encoder_1_out));

  // Notes on the sheet:
  //   不要改变此引脚区域内容，也不要改变ALU封装形式
  //   输入引脚
  //   输出引脚
endmodule

// 中断控制器
module \中断控制器  (
  input  CLK,
  input  Key1,
  input  Key2,
  input  Key3,
  input  Clr,
  input  [1:0] EDU_TEST,
  output IR1W,
  output IR2W,
  output IR3W,
  output [1:0] IntNo,
  output IntR
);

  wire and_1_out, and_2_out, and_3_out, Clr0, Clr1, Clr2, Clr3, d_ff_1_q, d_ff_2_q, d_ff_3_q, IR1_q, IR2_q,
       IR3_q, or_1_out, or_3_out, or_6_out, or_7_out, or_8_out;

  or or_1 (or_1_out, Key1, EDU_TEST[0]);
  or or_2 (IR1W, IR1_q, d_ff_2_q);
  or or_3 (or_3_out, Key2, EDU_TEST[1]);
  or or_4 (IR2W, IR2_q, d_ff_3_q);
  D_Flip_Flop #(.trigger("rising"), .Pre_Clr_Positions("LEGACY"), .NegatePresetClear("false"), .enable("true"), .NewFFLayout("false")) d_ff_1 (
    .clk(Key3), .D(1'b1), .Q(d_ff_1_q), .reset(IR3_q));  // open: Qn, preset, en
  or or_5 (IR3W, IR3_q, d_ff_1_q);
  D_Flip_Flop #(.trigger("rising"), .Pre_Clr_Positions("LEGACY"), .NegatePresetClear("false"), .enable("true"), .NewFFLayout("false")) d_ff_2 (
    .clk(or_1_out), .D(1'b1), .Q(d_ff_2_q), .reset(IR1_q));  // open: Qn, preset, en
  D_Flip_Flop #(.trigger("rising"), .Pre_Clr_Positions("LEGACY"), .NegatePresetClear("false"), .enable("true"), .NewFFLayout("false")) d_ff_3 (
    .clk(or_3_out), .D(1'b1), .Q(d_ff_3_q), .reset(IR2_q));  // open: Qn, preset, en
  or or_6 (or_6_out, d_ff_2_q, IR1_q);
  and and_1 (and_1_out, or_6_out, ~Clr1);  // AND_Gate
  or or_7 (or_7_out, d_ff_3_q, IR2_q);
  and and_2 (and_2_out, or_7_out, ~Clr2);  // AND_Gate
  or or_8 (or_8_out, d_ff_1_q, IR3_q);
  and and_3 (and_3_out, or_8_out, ~Clr3);  // AND_Gate
  Pull_Resistor #(.pull(0)) pull_resistor_1 (.node(EDU_TEST));
  D_Flip_Flop #(.trigger("rising"), .Pre_Clr_Positions("LEGACY"), .NegatePresetClear("false"), .enable("true"), .NewFFLayout("false")) IR1 (
    .clk(CLK), .D(and_1_out), .Q(IR1_q));  // open: Qn, preset, en, reset
  D_Flip_Flop #(.trigger("rising"), .Pre_Clr_Positions("LEGACY"), .NegatePresetClear("false"), .enable("true"), .NewFFLayout("false")) IR2 (
    .clk(CLK), .D(and_2_out), .Q(IR2_q));  // open: Qn, preset, en, reset
  D_Flip_Flop #(.trigger("rising"), .Pre_Clr_Positions("LEGACY"), .NegatePresetClear("false"), .enable("true"), .NewFFLayout("false")) IR3 (
    .clk(CLK), .D(and_3_out), .Q(IR3_q));  // open: Qn, preset, en, reset
  Priority_Encoder #(.select(2), .disabled("Z")) priority_encoder_1 (
    .in1(IR1_q), .in2(IR2_q), .in3(IR3_q), .out(IntNo), .gs(IntR));  // open: in0, en_out, en_in
  Decoder #(.select(2), .tristate("false"), .disabled(0), .enable("true")) decoder_1 (
    .out0(Clr0), .out1(Clr1), .out2(Clr2), .out3(Clr3), .sel(IntNo), .en(Clr));

  // Other names for the same wires on the sheet: EDU_INT1 = EDU_TEST[0]; EDU_INT2 = EDU_TEST[1]

  // Notes on the sheet:
  //   中断等待
  //   中断等待
  //   中断等待
  //   中断信号采样参考电路
  //   Reset 
  //   Reset 
  //   Reset 
  //   中断优先编码器
endmodule
